// Logisim project Summary of types of gate.circ as structural Verilog: 1 circuit, main circuit main
module main (
);

  wire _1_2_out, _1_3_out, _1_out, _2_2_out, _2_3_out, _2_out, _3_2_out, _3_3_out, _3_out, _4_2_out,
       _4_3_out, _4_out, _5_2_out, _5_out, _6_2_out, _6_out, _7_2_out, _7_out, _8_2_out, _8_out, _9_2_out,
       _9_out, _10_out, _11_out, _12_out, _13_out, _14_out, and_1_out, and_2_out, and_3_out, nand_1_out,
       nand_2_out, nand_3_out, nand_4_out, nand_5_out, nand_6_out, nand_7_out, nand_8_out, nand_9_out,
       nand_10_out, nand_11_out, nand_12_out, nand_13_out, nand_14_out, nand_15_out, nand_16_out,
       nand_17_out, nand_18_out, nand_19_out, nand_20_out, nand_21_out, nand_22_out, nand_23_out,
       nand_24_out, nand_25_out, nand_26_out, nand_27_out, not_1_out, not_2_out, not_3_out, not_4_out,
       not_5_out, xnor_1_out, xnor_2_out;

  not not_1 (not_1_out, 1'b0);
  not not_2 (not_2_out, 1'b0);
  not not_3 (not_3_out, 1'b0);
  and and_1 (and_1_out, 1'b1, 1'b1);
  and and_2 (and_2_out, 1'b1, not_1_out);
  and and_3 (and_3_out, not_2_out, not_3_out);
  nand _1 (_1_out, 1'b0, 1'b0);
  not not_4 (not_4_out, 1'b1);
  not not_5 (not_5_out, 1'b1);
  // Probe on xnor_1_out
  xnor xnor_1 (xnor_1_out, 1'b1, 1'b1);
  // Probe on xnor_2_out
  xnor xnor_2 (xnor_2_out, 1'b1, 1'b1);
  // Probe on and_1_out
  // Probe on and_2_out
  // Probe on and_3_out
  nand nand_1 (nand_1_out, 1'b1, not_4_out);
  nand nand_2 (nand_2_out, 1'b1, not_5_out);
  // Probe on nand_3_out
  nand nand_3 (nand_3_out, 1'b1, nand_4_out);
  // Probe on nand_4_out
  nand nand_4 (nand_4_out, nand_3_out, 1'b1);
  nand nand_5 (nand_5_out, 1'b0, 1'b0);
  nand nand_6 (nand_6_out, 1'b0, 1'b0);
  nand _2 (_2_out, 1'b0, _1_out);
  nand _3 (_3_out, _1_out, 1'b0);
  nand nand_7 (nand_7_out, nand_1_out, nand_2_out);
  // Probe on nand_7_out
  nand nand_8 (nand_8_out, nand_5_out, nand_6_out);
  // Probe on nand_8_out
  nand _4 (_4_out, _2_out, _3_out);
  nand _5 (_5_out, _4_out, 1'b1);
  nand nand_9 (nand_9_out, 1'b1, 1'b1);
  nand nand_10 (nand_10_out, nand_9_out, 1'b1);
  nand nand_11 (nand_11_out, 1'b1, 1'b0);
  nand nand_12 (nand_12_out, 1'b0, 1'b1);
  nand _6 (_6_out, _4_out, _5_out);
  nand _7 (_7_out, _5_out, 1'b1);
  nand _8 (_8_out, _5_out, _1_out);
  nand _1_2 (_1_2_out, 1'b1, 1'b1);
  nand nand_13 (nand_13_out, 1'b1, 1'b1);
  nand nand_14 (nand_14_out, 1'b1, 1'b1);
  // Probe on _8_out
  // Probe on nand_15_out
  nand nand_15 (nand_15_out, nand_9_out, nand_16_out);
  // Probe on nand_16_out
  nand nand_16 (nand_16_out, nand_15_out, nand_10_out);
  nand nand_17 (nand_17_out, 1'b1, nand_11_out);
  nand nand_18 (nand_18_out, nand_11_out, 1'b0);
  nand nand_19 (nand_19_out, 1'b0, nand_12_out);
  nand nand_20 (nand_20_out, nand_12_out, 1'b1);
  nand nand_21 (nand_21_out, 1'b1, nand_14_out);
  nand nand_22 (nand_22_out, nand_14_out, 1'b1);
  nand nand_23 (nand_23_out, nand_14_out, nand_14_out);
  nand _9 (_9_out, _6_out, _7_out);
  // Probe on _9_out
  nand _2_2 (_2_2_out, 1'b1, _1_2_out);
  nand _3_2 (_3_2_out, 1'b1, nand_13_out);
  nand nand_24 (nand_24_out, nand_17_out, nand_18_out);
  // Probe on nand_24_out
  nand nand_25 (nand_25_out, nand_19_out, nand_20_out);
  nand nand_26 (nand_26_out, nand_21_out, nand_22_out);
  // Probe on nand_23_out
  nand _4_2 (_4_2_out, _2_2_out, _3_2_out);
  // Probe on _4_2_out
  nand nand_27 (nand_27_out, nand_25_out, nand_25_out);
  // Probe on nand_26_out
  // Probe on nand_27_out
  nand _1_3 (_1_3_out, 1'b1, 1'b1);
  nand _2_3 (_2_3_out, 1'b1, 1'b1);
  nand _3_3 (_3_3_out, 1'b1, _1_3_out);
  nand _4_3 (_4_3_out, 1'b1, _2_3_out);
  nand _5_2 (_5_2_out, _3_3_out, _4_3_out);
  nand _6_2 (_6_2_out, 1'b1, _5_2_out);
  nand _7_2 (_7_2_out, 1'b1, _6_2_out);
  nand _8_2 (_8_2_out, _6_2_out, _5_2_out);
  nand _9_2 (_9_2_out, _7_2_out, _8_2_out);
  nand _10 (_10_out, _9_2_out, 1'b1);
  nand _11 (_11_out, _9_2_out, _10_out);
  nand _12 (_12_out, _10_out, 1'b1);
  nand _13 (_13_out, _10_out, _6_2_out);
  // Probe on _14_out
  nand _14 (_14_out, _11_out, _12_out);
  // Probe on _13_out

  // Notes on the sheet:
  //   A
  //   B
  //   C
  //   XOR Gate
  //   XNOR Gate
  //   2:1 Multiplexer
  //   SR Latch
  //   NAND based OR gate
  //   NAND based Full Adder
  //   C
  //   B
  //   D Latch
  //   NAND based XOR Gate
  //   NAND based XNOR Gate
  //   NAND based Half Adder
  //   NAND based 2:1 Multiplexer 
  //   B
  //   C
  //   B
  //   NAND based 2:1 Multiplexer 
  //   Full AdderSubtractor
  //   A
  //   NAND based Full Adder
endmodule
