// Logisim project Latches131014.circ as structural Verilog: 1 circuit, main circuit main
module main (
);

  wire nand_1_out, nand_2_out, nand_3_out, nand_4_out, nand_5_out, nand_6_out;

  nand nand_1 (nand_1_out, 1'b0, nand_2_out);
  nand nand_2 (nand_2_out, nand_1_out, 1'b1);
  nand nand_3 (nand_3_out, 1'b1, 1'b0);
  nand nand_4 (nand_4_out, nand_3_out, 1'b0);
  // Probe on nothing
  // Probe on nothing
  nand nand_5 (nand_5_out, nand_3_out, nand_6_out);
  nand nand_6 (nand_6_out, nand_5_out, nand_4_out);
  // Probe on nothing
  // Probe on nothing

  // Notes on the sheet:
  //   D
  //   E
  //   Q
  //   Set Reset Latch
  //   Q'
  //   Q
  //   D Latch
  //   Q'
endmodule
