// Logisim project lab1 Logism.circ as structural Verilog: 1 circuit, main circuit main
module main (
);

  wire transistor_1_out, transistor_2_out, transistor_4_out, transistor_5_out, transistor_9_out,
       transistor_11_out, transistor_12_out, transistor_13_out, transistor_14_out, transistor_16_out,
       transistor_21_out;

  Transistor transistor_1 (.in(1'b1), .out(transistor_1_out), .gate(1'b1));
  Transistor transistor_2 (.in(transistor_4_out), .out(transistor_2_out), .gate(1'b1));
  Transistor #(.\type ("n")) transistor_3 (.in(1'b1), .out(transistor_2_out), .gate(1'b1));
  Transistor transistor_4 (.in(1'b0), .out(transistor_4_out), .gate(1'b1));
  Transistor transistor_5 (.in(1'b1), .out(transistor_5_out), .gate(1'b0));
  Transistor #(.\type ("n")) transistor_6 (.in(1'b0), .out(transistor_5_out), .gate(1'b0));
  Transistor transistor_7 (.in(1'b1), .out(transistor_1_out), .gate(1'b0));
  // Probe on transistor_1_out
  Transistor #(.\type ("n")) transistor_8 (.in(transistor_9_out), .out(transistor_1_out), .gate(1'b0));
  Transistor #(.\type ("n")) transistor_9 (.in(1'b0), .out(transistor_9_out), .gate(1'b1));
  Transistor #(.\type ("n")) transistor_10 (.in(1'b1), .out(transistor_2_out), .gate(1'b1));
  // Probe on transistor_2_out
  // Probe on transistor_5_out
  Transistor transistor_11 (.in(1'b0), .out(transistor_11_out), .gate(1'b0));
  Transistor transistor_12 (.in(1'b1), .out(transistor_12_out), .gate(1'b1));
  Transistor transistor_13 (.in(1'b1), .out(transistor_13_out), .gate(1'b0));
  Transistor #(.\type ("n")) transistor_14 (.in(1'b0), .out(transistor_14_out), .gate(1'b0));
  Transistor transistor_15 (.in(transistor_13_out), .out(transistor_14_out), .gate(1'b1));
  Transistor #(.\type ("n")) transistor_16 (.in(1'b1), .out(transistor_16_out), .gate(1'b0));
  Transistor #(.\type ("n")) transistor_17 (.in(transistor_16_out), .out(transistor_11_out), .gate(1'b1));
  Transistor transistor_18 (.in(1'b0), .out(transistor_11_out), .gate(1'b1));
  // Probe on transistor_11_out
  // Probe on transistor_12_out
  Transistor transistor_19 (.in(1'b1), .out(transistor_12_out), .gate(1'b1));
  Transistor #(.\type ("n")) transistor_20 (.in(transistor_21_out), .out(transistor_12_out), .gate(1'b1));
  Transistor #(.\type ("n")) transistor_21 (.in(1'b0), .out(transistor_21_out), .gate(1'b1));
  Transistor #(.\type ("n")) transistor_22 (.in(1'b0), .out(transistor_14_out), .gate(1'b1));
  // Probe on transistor_14_out

  // Notes on the sheet:
  //   A
  //   B
  //   A
  //   NAND Gate
  //   B
  //   NAND Gate N on top
  //   NOT Gate
  //   A
  //   B
  //   A
  //   B
  //   NOR Gate
  //   NOR Gate N on top
  //   NAND Gate with NOT Logic
endmodule
